# Fritzing sketch Frontbord2 (saved by Fritzing 0.9.3b)
circuit board: 7.5cm x 1.8cm
breadboards: 1

parts:
  J2 = female pin header, 1 pin [form="♀ (female)"]
  J3 = female pin header, 1 pin [form="♀ (female)"]
  J4 = female pin header, 1 pin [form="♀ (female)"]
  J5 = female pin header, 1 pin [form="♀ (female)"]
  J6 = female pin header, 1 pin [form="♀ (female)"]
  J7 = female pin header, 3 pins [form="♀ (female)"]
  J8 = female pin header, 3 pins [form="♀ (female)"]
  J9 = female pin header, 4 pins [form="♀ (female)"]
  J10 = female pin header, 4 pins [form="♀ (female)"]
  J12 = female pin header, 4 pins [form="♀ (female)"]
  J13 = female pin header, 4 pins [form="♀ (female)"]
  J14 = female pin header, 4 pins [form="♀ (female)"]
  J15 = female pin header, 2 pins [form="♀ (female)"]
  J1 = female pin header, 3 pins [form="♀ (female)"]

nets:
  N1: J2.pin1, J1.pin1, J1.pin2, J1.pin3
  N2: J3.pin1, J7.pin1, J7.pin2, J7.pin3
  N3: J4.pin1, J9.pin1, J9.pin2, J9.pin3, J9.pin4
  N4: J5.pin1, J8.pin1, J8.pin2, J8.pin3
  N5: J6.pin1, J10.pin1, J10.pin2, J10.pin3, J10.pin4, J13.pin4, J14.pin4, J15.pin1, J15.pin2
  N6: J12.pin1, J12.pin2, J12.pin3, J12.pin4, J13.pin1, J14.pin1
  N7: J13.pin2, J14.pin2
  N8: J13.pin3, J14.pin3

notes:
  pin0
  pin1
  pin2
  3volt
  -GND-
  5volt
  V Data G
  micro:bit servo extension bord
