# Fritzing sketch ServoFrontboard met servo pins - v0.4 (saved by Fritzing 0.9.3b)
circuit board: 6.80001cm x 2.59999cm
breadboards: 1

parts:
  J2 = female pin header, 1 pin [form="♀ (female)"]
  J3 = female pin header, 1 pin [form="♀ (female)"]
  J4 = female pin header, 1 pin [form="♀ (female)"]
  J5 = female pin header, 1 pin [form="♀ (female)"]
  J7 = female pin header, 3 pins [form="♀ (female)"]
  J8 = female pin header, 3 pins [form="♀ (female)"]
  J9 = female pin header, 4 pins [form="♀ (female)"]
  J10 = female pin header, 4 pins [form="♀ (female)"]
  J12 = female pin header, 4 pins [form="♀ (female)"]
  J13 = female pin header, 4 pins [form="♀ (female)"]
  J14 = female pin header, 4 pins [form="♀ (female)"]
  J15 = female pin header, 2 pins [form="♀ (female)"]
  J1 = female pin header, 3 pins [form="♀ (female)"]
  J16 = female pin header, 3 pins [form="♀ (female)"]
  J17 = female pin header, 3 pins [form="♀ (female)"]
  J18 = female pin header, 3 pins [form="♀ (female)"]
  J20 = female pin header, 1 pin [form="♀ (female)"]
  J21 = female pin header, 1 pin [form="♀ (female)"]
  J22 = female pin header, 2 pins [form="♀ (female)"]
  J24 = female pin header, 1 pin [form="♀ (female)"]
  C1 = Capacitor Polarized [package=cpol-radial-100uf-25v]
  J6 = female pin header, 1 pin [form="♀ (female)"]

nets:
  N1: J2.pin1, J1.pin1, J1.pin2, J1.pin3, J16.pin3
  N2: J3.pin1, J7.pin1, J7.pin2, J7.pin3, J18.pin3
  N3: J4.pin1, J9.pin1, J9.pin2, J9.pin3, J9.pin4, J17.pin3
  N4: J5.pin1, J8.pin1, J8.pin2, J8.pin3
  N5: J10.pin1, J10.pin2, J10.pin3, J10.pin4, J13.pin4, J14.pin4, J15.pin1, J15.pin2, J16.pin1, J17.pin1, J18.pin1, J21.pin1, J22.pin1, J24.pin1, J6.pin1
  N6: J12.pin1, J12.pin2, J12.pin3, J12.pin4, J13.pin1, J14.pin1, J16.pin2, J17.pin2, J18.pin2, C1.+
  N7: J13.pin2, J14.pin2
  N8: J13.pin3, J14.pin3
  N9: J20.pin1, J22.pin2, C1.-

notes:
  pin0
  pin1
  pin2
  3volt
  -GND-
  5volt
  V Data G
  front board
  5V
  GND
  S
  micro:bit
  2019-05-30
  Hans de Jong
