# Fritzing sketch ServoPCB straight v0.6 (saved by Fritzing 0.9.3b)
circuit board: 1.6cm x 3.09999cm
breadboards: 1

parts:
  J10 = male pin header, 4 pins [form="♂ (male)"]
  J9 = male pin header, 4 pins [form="♂ (male)"]
  J12 = male pin header, 5 pins [form="♂ (male)"]
  J11 = male pin header, 5 pins [form="♂ (male)"]
  J4 = male pin header, 5 pins [form="♂ (male)"]
  J13 = male pin header, 5 pins [form="♂ (male)"]

nets:
  N1: J10.pin1, J9.pin1, J12.pin3, J11.pin3, J4.pin3, J13.pin1, J13.pin2, J13.pin3
  N2: J10.pin2, J9.pin2
  N3: J10.pin3, J9.pin3
  N4: J10.pin4, J9.pin4, J4.pin5
  N5: J12.pin1, J12.pin2
  N6: J12.pin4, J12.pin5, J11.pin4, J11.pin5, J4.pin4, J13.pin4, J13.pin5
  N7: J11.pin1, J11.pin2
  N8: J4.pin1, J4.pin2

notes:
  V
  G
  S
  Data
  -Servos-
  jumper
  tywrap
  m:b
  micro:bit servo bord
  <-servo->
  3x
