# Fritzing sketch ServoPCB with microUSB v0.1 (saved by Fritzing 0.9.3b)
circuit board: 1.54778cm x 4.83709cm
breadboards: 1

parts:
  J10 = male pin header, 4 pins [form="♂ (male)"]
  J9 = male pin header, 4 pins [form="♂ (male)"]
  J12 = male pin header, 5 pins [form="♂ (male)"]
  J11 = male pin header, 5 pins [form="♂ (male)"]
  J4 = male pin header, 5 pins [form="♂ (male)"]
  J13 = male pin header, 5 pins [form="♂ (male)"]
  J29 = female pin header, 5 pins [form="♀ (female)"]
  J30 = female pin header, 1 pin [form="♀ (female)"]  # not connected
  J31 = female pin header, 1 pin [form="♀ (female)"]  # not connected
  J35 = male pin header, 1 pin [form="♂ (male)"]
  J36 = female pin header, 1 pin [form="♀ (female)"]
  J34 = female pin header, 1 pin [form="♀ (female)"]

nets:
  N1: J10.pin1, J9.pin1, J12.pin3, J11.pin3, J4.pin3, J13.pin1, J13.pin2, J13.pin3, J29.pin1, J35.pin1
  N2: J10.pin2, J9.pin2
  N3: J10.pin3, J9.pin3
  N4: J10.pin4, J9.pin4, J4.pin5, J29.pin5, J36.pin1, J34.pin1
  N5: J12.pin1, J12.pin2
  N6: J12.pin4, J12.pin5, J11.pin4, J11.pin5, J4.pin4, J13.pin4, J13.pin5
  N7: J11.pin1, J11.pin2
  N8: J4.pin1, J4.pin2

notes:
  V
  G
  S
  Data
  -Servos-
  jumper
  tywrap
  m:b
  micro:bit servo bord
  <-servo->
  3x
  VCC
  GND
  power socket
  5VoltIn
